# Fritzing sketch TapuinoNext (saved by Fritzing 0.9.7b)
breadboards: 1

parts:
  Part3 = I2C level shifter bidirectional
  R5 = Resistor [tolerance=±5% resistance=3.3k power=0.25 package=THT]
  RE2 = KY-040 Rotary encoder [package=THT]
  R6 = Resistor [tolerance=±5% resistance=1.5k power=0.25 package=THT]
  microSD_Transflash2 = SparkFun - microSD Transflash
  OLED_I2C2 = OLED 128x64 I2C Monochrome Display
  U2 = ESP32-38PinWide [part_number=ESP32-38PinWide]
  JP2 = Header 6 [package=1x06_smd_straight_alt]
  LED1 = LED - 5mm [color="Red (633nm)" current=0.030 package="5 mm [THT]"]
  R7 = Resistor [tolerance=±5% resistance=220 package="2512 [SMD]"]

nets:
  N1: Part3.LV4, U2.GPIO18
  N2: Part3.LV3, U2.GPIO5
  GND: Part3.GND, R5.Pin_0, RE2.GND, microSD_Transflash2.GND, microSD_Transflash2.CS, OLED_I2C2.GND, U2.GND, JP2.1, R7.Pin_1
  VCC: Part3.LV, RE2.Vcc, microSD_Transflash2.VCC, U2.3.3
  N3: Part3.LV2, U2.GPIO17
  N4: Part3.LV1, U2.GPIO16
  N5: Part3.HV1, JP2.6
  N6: Part3.HV2, R5.Pin_1, R6.Pin_0
  VDD: Part3.HV, OLED_I2C2.VDD, U2.VIN, JP2.2
  N7: Part3.HV3, JP2.4
  N8: Part3.HV4, JP2.5
  N9: RE2.SW, U2.GPIO32
  N10: RE2.DT, U2.GPIO33
  N11: RE2.CLK, U2.GPIO25
  N12: R6.Pin_1, JP2.3
  N13: microSD_Transflash2.DO, U2.GPIO2
  N14: microSD_Transflash2.SCK, U2.GPIO14
  N15: microSD_Transflash2.DI, U2.GPIO15
  N16: OLED_I2C2.SDA, U2.GPIO21
  N17: OLED_I2C2.SCK, U2.GPIO22
  N18: U2.GPIO23, LED1.anode
  N19: LED1.cathode, R7.Pin_0

notes:
  v0.4
  Original by Attila Gabriel, fixes by sweetlilmre
  +5V Red wire
  +3.3V Orange wire
  C64 TAPE Connector
  1. Black => C64 Datasette GND
  2. Red => C64 Datasette 5V
  3. Pink => C64 Datasette Motor
  4. Yellow => C64 Datasette Read
  5. White => C64 Datasette Write
  6. Blue => C64 Datasette Sense

custom parts:
  KY-040 Rotary encoder: KY-040 Rotary Encoder with switch on breakout borad from AZ Delivery
  ESP32-38PinWide: Generic 38-Pin ESP32 with wide format (only access to one side of pins on a breadboard) based on Stephen Lilley's HiLetgo ESP-WROOM-32 ESP32 ESP-32S Development Board.
